// Logisim project CEFinal.circ as structural Verilog: 5 circuits, main circuit main
module main (
  input  [1:0] in_1,
  input  in_2,
  input  [7:0] in_3,
  input  in_4
);

  wire and_1_out, clock_1_out, decoder_1_out2, decoder_1_out3, decoder_1_out4, decoder_1_out6,
       decoder_1_out7, not_1_out, not_2_out, or_1_out, or_2_out;
  wire [1:0] and_2_out;
  wire [3:0] multiplexer_3_out;
  wire [7:0] alu_v4_1_out, alu_v4_2_out, bit_extender_1_out, multiplexer_1_out, multiplexer_2_out,
       ram_1_data, register_1_q, register_file_1_read_data_1, register_file_1_read_data_2;
  wire [15:0] rom_1_data;

  Register register_1 (.D(alu_v4_1_out), .Q(register_1_q), .clk(clock_1_out));  // open: en, clr
  ALU_v4 alu_v4_1 (.control(in_1), .A(in_3), .B(register_1_q), .in_1(in_2), .out(alu_v4_1_out));  // open: overflow
  ROM #(.dataWidth(16)) rom_1 (.addr(register_1_q), .data(rom_1_data));  // open: sel
  Clock clock_1 (.out(clock_1_out));
  Decoder #(.select(3), .enable("false")) decoder_1 (
    .out2(decoder_1_out2), .out3(decoder_1_out3), .out4(decoder_1_out4), .out6(decoder_1_out6),
    .out7(decoder_1_out7), .sel(rom_1_data[2:0]));  // open: out0, out1, out5
  Multiplexer #(.width(8), .enable("false")) multiplexer_1 (
    .in0(ram_1_data), .in1(alu_v4_2_out), .out(multiplexer_1_out), .sel(not_2_out));
  Register_File register_file_1 (
    .data_in_from_ALU(multiplexer_1_out), .write_control(or_1_out), .choose_reg(rom_1_data[7:4]),
    .clk(clock_1_out), .read_data_1(register_file_1_read_data_1), .choose_reg___1(rom_1_data[11:8]),
    .read_data_2(register_file_1_read_data_2), .choose_reg__2(rom_1_data[15:12]));
  ALU_v4 alu_v4_2 (
    .control(and_2_out), .A(multiplexer_2_out), .B(register_file_1_read_data_1), .in_1(in_4),
    .out(alu_v4_2_out));  // open: overflow
  or or_1 (or_1_out, decoder_1_out2, decoder_1_out3, decoder_1_out4, decoder_1_out6, decoder_1_out7);
  not not_1 (not_1_out, decoder_1_out3);
  and and_1 (and_1_out, not_1_out, decoder_1_out2);
  Multiplexer #(.width(8), .enable("false")) multiplexer_2 (
    .in0(register_file_1_read_data_2), .in1(bit_extender_1_out), .out(multiplexer_2_out), .sel(or_2_out));
  or or_2 (or_2_out, decoder_1_out2, decoder_1_out3);
  assign bit_extender_1_out = {{4{1'b0}}, multiplexer_3_out};  // Bit_Extender bit_extender_1
  Multiplexer #(.width(4), .enable("false")) multiplexer_3 (
    .in0(rom_1_data[15:12]), .in1(rom_1_data[7:4]), .out(multiplexer_3_out), .sel(and_1_out));
  RAM #(.bus("separate")) ram_1 (
    .addr(alu_v4_2_out), .din(register_file_1_read_data_2), .data(ram_1_data), .str(decoder_1_out3),
    .clk(clock_1_out), .ld(decoder_1_out2));  // open: sel, clr
  not not_2 (not_2_out, decoder_1_out2);
  or or_3 (and_2_out[1], decoder_1_out2, decoder_1_out3, decoder_1_out4);
  not not_3 (decoder_1_out6, decoder_1_out6);
  and and_2 (and_2_out[0], decoder_1_out6, decoder_1_out7);

  // Notes on the sheet:
  //   instruction memory
  //   splitting to make 3-bit opcode
  //   hardcode these to be adders
  //   contents of rom_1 (hex, n*v repeats v):
  //   12 22 12 22 1234 1344 1354 1454 1564 6703
  //   pass immediate for store into 1st mjux
  //   determine whether to take output from ALU or from data mem
  //   to see if it's load vs store
  //   mux to choose between computing for load/store vs computing for add/or/and
endmodule

module _1_bit_adder_12_8_19 (
  input  A,
  input  B,
  input  Cin0,
  output sum,
  output Cout
);

  wire and_1_out, and_2_out, xor_1_out;

  xor xor_1 (xor_1_out, A, B);
  and and_1 (and_1_out, A, B);
  and and_2 (and_2_out, xor_1_out, Cin0);
  xor xor_2 (sum, xor_1_out, Cin0);
  or or_1 (Cout, and_1_out, and_2_out);

  // Notes on the sheet:
  //   XOR gate for a+b
  //   (a+b) && carryIN
  //   (a+b)+carryIN
  //   a && b
  //   carryOut
  //   Cout0=Cin1
endmodule

module _1_bit_ALU_12_8_19 (
  input  A,
  input  B,
  input  [1:0] Control_Statement,
  input  Cin,
  output Out,
  output Cout
);

  wire _1_bit_adder_sum, and_1_out, or_1_out;

  _1_bit_adder_12_8_19 _1_bit_adder (.A(A), .B(B), .Cin0(Cin), .sum(_1_bit_adder_sum), .Cout(Cout));
  or or_1 (or_1_out, A, B);
  and and_1 (and_1_out, A, B);
  Multiplexer #(.select(2)) multiplexer_1 (
    .in0(or_1_out), .in1(and_1_out), .in2(_1_bit_adder_sum), .out(Out), .sel(Control_Statement));  // open: in3, en

  // Notes on the sheet:
  //   idea for ALU with 4:1 multiplexer
  //   3 inputs, 1 unused input, 1 output
  //   making an ALU that returns values for A*B, A+B, and Cout
  //   feed both versions of ALU into the 8-bit?
  //   00 = OR
  //   01 = AND
  //   10=ADD
endmodule

module ALU_v4 (
  input  in_1,
  input  [7:0] A,
  input  [7:0] B,
  input  [1:0] control,
  output [7:0] out,
  output overflow
);

  wire _0_cout, _1_cout, _2_cout, _3_cout, _4_cout, _5_cout, _6_cout;

  _1_bit_ALU_12_8_19 _0 (.A(A[0]), .B(B[0]), .Cin(in_1), .Out(out[0]), .Cout(_0_cout), .Control_Statement(control));
  _1_bit_ALU_12_8_19 _1 (.A(A[1]), .B(B[1]), .Cin(_0_cout), .Out(out[1]), .Cout(_1_cout), .Control_Statement(control));
  _1_bit_ALU_12_8_19 _2 (.A(A[2]), .B(B[2]), .Cin(_1_cout), .Out(out[2]), .Cout(_2_cout), .Control_Statement(control));
  _1_bit_ALU_12_8_19 _3 (.A(A[3]), .B(B[3]), .Cin(_2_cout), .Out(out[3]), .Cout(_3_cout), .Control_Statement(control));
  _1_bit_ALU_12_8_19 _4 (.A(A[4]), .B(B[4]), .Cin(_3_cout), .Out(out[4]), .Cout(_4_cout), .Control_Statement(control));
  _1_bit_ALU_12_8_19 _5 (.A(A[5]), .B(B[5]), .Cin(_4_cout), .Out(out[5]), .Cout(_5_cout), .Control_Statement(control));
  _1_bit_ALU_12_8_19 _6 (.A(A[6]), .B(B[6]), .Cin(_5_cout), .Out(out[6]), .Cout(_6_cout), .Control_Statement(control));
  _1_bit_ALU_12_8_19 _7 (.A(A[7]), .B(B[7]), .Cin(_6_cout), .Out(out[7]), .Cout(overflow), .Control_Statement(control));
endmodule

module Register_File (
  input  write_control,
  input  [3:0] choose_reg___1,
  input  [7:0] data_in_from_ALU,
  input  [3:0] choose_reg,
  input  [3:0] choose_reg__2,
  input  clk,
  output [7:0] read_data_1,
  output [7:0] read_data_2
);

  wire and_1_out, and_2_out, and_3_out, and_4_out, and_5_out, decoder_1_out0, decoder_1_out1, decoder_1_out2,
       decoder_1_out3, decoder_1_out4, undriven;
  wire [7:0] demultiplexer_1_out0, demultiplexer_1_out1, demultiplexer_1_out2, demultiplexer_1_out3,
       demultiplexer_1_out4, demultiplexer_1_out5, demultiplexer_1_out6, demultiplexer_1_out7,
       demultiplexer_1_out8, demultiplexer_1_out9, demultiplexer_1_out10, demultiplexer_1_out11,
       demultiplexer_1_out12, demultiplexer_1_out13, demultiplexer_1_out14, demultiplexer_1_out15,
       register_1_q, register_2_q, register_3_q, register_4_q, register_5_q, register_6_q, register_7_q,
       register_8_q, register_9_q, register_10_q, register_11_q, register_12_q, register_13_q, register_14_q,
       register_15_q, register_16_q;

  Decoder #(.select(4)) decoder_1 (
    .out0(decoder_1_out0), .out1(decoder_1_out1), .out2(decoder_1_out2), .out3(decoder_1_out3),
    .out4(decoder_1_out4), .sel(choose_reg));  // open: out5, out6, out7, out8, out9, out10, out11, out12, out13, out14, out15, en
  Demultiplexer #(.select(4), .width(8), .enable("false")) demultiplexer_1 (
    .out0(demultiplexer_1_out0), .out1(demultiplexer_1_out1), .out2(demultiplexer_1_out2),
    .out3(demultiplexer_1_out3), .out4(demultiplexer_1_out4), .out5(demultiplexer_1_out5),
    .out6(demultiplexer_1_out6), .out7(demultiplexer_1_out7), .out8(demultiplexer_1_out8),
    .out9(demultiplexer_1_out9), .out10(demultiplexer_1_out10), .out11(demultiplexer_1_out11),
    .out12(demultiplexer_1_out12), .out13(demultiplexer_1_out13), .out14(demultiplexer_1_out14),
    .out15(demultiplexer_1_out15), .in(data_in_from_ALU), .sel(choose_reg));
  and and_1 (and_1_out, write_control, decoder_1_out0);
  and and_2 (and_2_out, write_control, decoder_1_out1);
  and and_3 (and_3_out, write_control, decoder_1_out2);
  and and_4 (and_4_out, write_control, decoder_1_out3);
  and and_5 (and_5_out, write_control, decoder_1_out4);
  Register register_1 (.D(demultiplexer_1_out0), .en(and_1_out), .Q(register_1_q), .clk(clk));  // open: clr
  Register register_2 (.D(demultiplexer_1_out1), .en(and_2_out), .Q(register_2_q), .clk(clk));  // open: clr
  Register register_3 (.D(demultiplexer_1_out2), .en(and_3_out), .Q(register_3_q), .clk(clk));  // open: clr
  Register register_4 (.D(demultiplexer_1_out3), .en(and_4_out), .Q(register_4_q), .clk(clk));  // open: clr
  Register register_5 (.D(demultiplexer_1_out4), .en(and_5_out), .Q(register_5_q), .clk(clk));  // open: clr
  Register register_6 (.D(demultiplexer_1_out5), .en(undriven), .Q(register_6_q), .clk(clk));  // open: clr
  Register register_7 (.D(demultiplexer_1_out6), .en(undriven), .Q(register_7_q), .clk(clk));  // open: clr
  Register register_8 (.D(demultiplexer_1_out7), .en(undriven), .Q(register_8_q), .clk(clk));  // open: clr
  Register register_9 (.D(demultiplexer_1_out8), .en(undriven), .Q(register_9_q), .clk(clk));  // open: clr
  Register register_10 (.D(demultiplexer_1_out9), .en(undriven), .Q(register_10_q), .clk(clk));  // open: clr
  Register register_11 (.D(demultiplexer_1_out10), .en(undriven), .Q(register_11_q), .clk(clk));  // open: clr
  Register register_12 (.D(demultiplexer_1_out11), .en(undriven), .Q(register_12_q), .clk(clk));  // open: clr
  Register register_13 (.D(demultiplexer_1_out12), .en(undriven), .Q(register_13_q), .clk(clk));  // open: clr
  Register register_14 (.D(demultiplexer_1_out13), .en(undriven), .Q(register_14_q), .clk(clk));  // open: clr
  Register register_15 (.D(demultiplexer_1_out14), .en(undriven), .Q(register_15_q), .clk(clk));  // open: clr
  Register register_16 (.D(demultiplexer_1_out15), .en(undriven), .Q(register_16_q), .clk(clk));  // open: clr
  Multiplexer #(.select(4), .width(8), .enable("false")) multiplexer_1 (
    .in0(register_1_q), .in1(register_2_q), .in2(register_3_q), .in3(register_4_q), .in4(register_5_q),
    .in5(register_6_q), .in6(register_7_q), .in7(register_8_q), .in8(register_9_q), .in9(register_10_q),
    .in10(register_11_q), .in11(register_12_q), .in12(register_13_q), .in13(register_14_q),
    .in14(register_15_q), .in15(register_16_q), .out(read_data_1), .sel(choose_reg___1));
  Multiplexer #(.select(4), .width(8)) multiplexer_2 (
    .in0(register_1_q), .in1(register_2_q), .in2(register_3_q), .in3(register_4_q), .in4(register_5_q),
    .in5(register_6_q), .in6(register_7_q), .in7(register_8_q), .in8(register_9_q), .in9(register_10_q),
    .in10(register_11_q), .in11(register_12_q), .in12(register_13_q), .in13(register_14_q),
    .in14(register_15_q), .in15(register_16_q), .out(read_data_2), .sel(choose_reg__2));  // open: en

  // Notes on the sheet:
  //   0
  //   1
  //   2
  //   3
  //   4
  //   5
  //   6
  //   7
  //   8
  //   9
  //   10
  //   11
  //   12
  //   13
  //   14
  //   15
  //   chooses rs1
  //   chooses rs2
endmodule
